// Logisim project Pipelined_CPU.circ as structural Verilog: 10 circuits, main circuit New_main
module _16_bit_register_file (
  input  Reset,
  input  [2:0] Read_Reg_1,
  input  [2:0] Read_Reg_2,
  input  Write,
  input  [2:0] Write_Reg_Destination,
  input  [15:0] Write_Data,
  output [15:0] Read_Reg_1_Output,
  output [15:0] Read_Reg_2_Output
);

  wire demultiplexer_1_out0, demultiplexer_1_out1, demultiplexer_1_out2, demultiplexer_1_out3,
       demultiplexer_1_out4, demultiplexer_1_out5, demultiplexer_1_out6, demultiplexer_1_out7;
  wire [15:0] r0_q, r1_q, r2_q, r3_q, r4_q, r5_q, r6_q;

  Demultiplexer #(.select(3)) demultiplexer_1 (
    .out0(demultiplexer_1_out0), .out1(demultiplexer_1_out1), .out2(demultiplexer_1_out2),
    .out3(demultiplexer_1_out3), .out4(demultiplexer_1_out4), .out5(demultiplexer_1_out5),
    .out6(demultiplexer_1_out6), .out7(demultiplexer_1_out7), .in(Write), .sel(Write_Reg_Destination));  // open: en
  Register #(.width(16)) r0 (.D(Write_Data), .Q(r0_q), .clk(demultiplexer_1_out0), .clr(Reset));  // open: en
  Register #(.width(16)) r1 (.D(Write_Data), .Q(r1_q), .clk(demultiplexer_1_out1), .clr(Reset));  // open: en
  Register #(.width(16)) r2 (.D(Write_Data), .Q(r2_q), .clk(demultiplexer_1_out2), .clr(Reset));  // open: en
  Register #(.width(16)) r3 (.D(Write_Data), .Q(r3_q), .clk(demultiplexer_1_out3), .clr(Reset));  // open: en
  Register #(.width(16)) r4 (.D(Write_Data), .Q(r4_q), .clk(demultiplexer_1_out4), .clr(Reset));  // open: en
  Register #(.width(16)) r5 (.D(Write_Data), .Q(r5_q), .clk(demultiplexer_1_out5), .clr(Reset));  // open: en
  Register #(.width(16)) r6 (.D(Write_Data), .Q(r6_q), .clk(demultiplexer_1_out6), .clr(Reset));  // open: en
  Register #(.width(16)) r7 (.D(Write_Data), .Q(r3_q), .clk(demultiplexer_1_out7), .clr(Reset));  // open: en
  Multiplexer #(.select(3), .width(16), .enable("false")) multiplexer_1 (
    .in0(r0_q), .in1(r1_q), .in2(r2_q), .in3(r3_q), .in4(r4_q), .in5(r5_q), .in6(r6_q), .in7(r3_q),
    .out(Read_Reg_1_Output), .sel(Read_Reg_1));
  Multiplexer #(.select(3), .width(16), .enable("false")) multiplexer_2 (
    .in0(r0_q), .in1(r1_q), .in2(r2_q), .in3(r3_q), .in4(r4_q), .in5(r5_q), .in6(r6_q), .in7(r3_q),
    .out(Read_Reg_2_Output), .sel(Read_Reg_2));
endmodule

module Instruction_Memory (
  input  [7:0] Address,
  output [15:0] Output
);

  ROM #(.dataWidth(16)) rom_1 (.addr(Address), .data(Output), .sel(1'b1));
endmodule

module Data_Memory (
  input  [7:0] Address,
  input  [15:0] Data_In,
  output [15:0] Data_Out
);

  RAM #(.dataWidth(16), .bus("separate")) ram_1 (
    .addr(Address), .din(Data_In), .data(Data_Out), .sel(1'b1));  // open: str, clk, ld, clr
endmodule

module ALU (
  input  [3:0] ALU_Op,
  input  [15:0] Input_A,
  input  [15:0] Input_B,
  output Zero,
  output [15:0] ALU_Output,
  output BorrowOut
);

  wire [15:0] adder_1_out, subtractor_1_out;

  Adder #(.width(16)) adder_1 (.a(Input_A), .b(Input_B), .out(adder_1_out));  // open: cin, cout
  Subtractor #(.width(16)) subtractor_1 (
    .a(Input_A), .b(Input_B), .out(subtractor_1_out), .bout(BorrowOut));  // open: bin
  Multiplexer #(.width(16), .enable("false")) multiplexer_1 (
    .in0(adder_1_out), .in1(subtractor_1_out), .out(ALU_Output), .sel(ALU_Op[1]));
  nor nor_1 (Zero, subtractor_1_out[0], subtractor_1_out[1], subtractor_1_out[2], subtractor_1_out[3], subtractor_1_out[4], subtractor_1_out[5], subtractor_1_out[6], subtractor_1_out[7], subtractor_1_out[8], subtractor_1_out[9], subtractor_1_out[10], subtractor_1_out[11], subtractor_1_out[12], subtractor_1_out[13], subtractor_1_out[14], subtractor_1_out[15]);

  // Notes on the sheet:
  //   Notes:
  //   uses bit 1 for add vs sub sel, bit 0 for imm vs reg field select
  //   For comparison use sub:
  //   ► a>b when zero=0, borrowout=0
  //   ► a<b when zero=0, borrowout=1
  //   only diff btw signed vs unsigned addition in how imm is sign extended, not relevant in ALU
  //   ► a=b when zero=1 (not 100% sure what borrowout reads in this case)
endmodule

module Sign_Extender (
  input  Unsigned,
  input  [7:0] Immediate,
  output [15:0] SignExtendedImm
);

  wire [15:0] bit_extender_1_out, bit_extender_2_out;

  assign bit_extender_1_out = {{8{Immediate[7]}}, Immediate};  // Bit_Extender bit_extender_1
  assign bit_extender_2_out = {{8{1'b0}}, Immediate};  // Bit_Extender bit_extender_2
  Multiplexer #(.width(16), .disabled(0), .enable("false")) multiplexer_1 (
    .in0(bit_extender_1_out), .in1(bit_extender_2_out), .out(SignExtendedImm), .sel(Unsigned));
endmodule

module New_main (
);

  wire button_1_out, clock_1_out, Decoder_p1, Decoder_p2, Decoder_p3, Decoder_p5, Decoder_p6, Decoder_p7,
       Decoder_p8, ex_mem_buffer_1_read_data_1_4, ex_mem_buffer_1_read_data_1_6,
       ex_mem_buffer_1_read_data_1_8, ex_mem_buffer_1_read_data_1_11, ex_mem_buffer_1_read_data_1_12,
       ex_mem_buffer_1_read_data_1_13, ex_mem_buffer_1_read_data_1_14, ex_mem_buffer_1_read_data_1_15,
       ex_mem_buffer_1_read_data_1_16, ex_mem_buffer_1_read_data_1_17, ID_EX_Buffer_out_35,
       ID_EX_Buffer_out_38, ID_EX_Buffer_out_41, ID_EX_Buffer_out_44, ID_EX_Buffer_out_45,
       ID_EX_Buffer_out_46, ID_EX_Buffer_out_48, ID_EX_Buffer_out_49, ID_EX_Buffer_out_50,
       ID_EX_Buffer_out_51, ID_EX_Buffer_out_52, ID_EX_Buffer_out_53, Instruction_Splitter_p2,
       Instruction_Splitter_p3, Instruction_Splitter_p4, Instruction_Splitter_p5, Instruction_Splitter_p7,
       Instruction_Splitter_p8, mem_wb_buffer_1_out_10, mem_wb_buffer_1_out_12, mem_wb_buffer_1_out_13,
       not_1_out, ResultToLess_p2, ResultToLess_p5, ResultToLess_p7, ResultToLess_p8, ResultToLess_p9,
       ResultToLess_p10, ResultToLess_p11, ResultToLess_p12, ResultToLess_p13;
  wire [1:0] undriven, undriven_2;
  wire [3:0] Decoder_p4, ex_mem_buffer_1_read_data_1_9, ID_EX_Buffer_out_39, ID_EX_Buffer_out_43,
       Instruction_Splitter_p6;
  wire [7:0] adder_1_out, ex_mem_buffer_1_out_21, ex_mem_buffer_1_read_data_1,
       ex_mem_buffer_1_read_data_1_10, ID_EX_Buffer_out_28, ID_EX_Buffer_out_29, ID_EX_Buffer_out_40,
       Instruction_Splitter_p9, multiplexer_4_out, multiplexer_5_out, PC_q, RegistertoAddress_2_p2,
       RegistertoAddress_p2;
  wire [15:0] alu_1_alu_output, bit_extender_1_out, ex_mem_buffer_1_read_data_1_3,
       ex_mem_buffer_1_read_data_1_5, ex_mem_buffer_1_read_data_1_7, ID_EX_Buffer_out_30,
       ID_EX_Buffer_out_31, ID_EX_Buffer_out_32, ID_EX_Buffer_out_36, ID_EX_Buffer_out_37,
       IF_ID_Buffer_out_3, mem_wb_buffer_1_out_8, mem_wb_buffer_1_out_9, mem_wb_buffer_1_out_11,
       multiplexer_1_out, multiplexer_2_out, multiplexer_3_out, multiplexer_7_out, multiplexer_8_out,
       ram_1_data, register_1_q, Registers_p4, Registers_p7, Registers_p8, ResultToLess_p1, rom_1_data,
       Shifter_p6, Sign_Extend_p3;

  not not_1 (not_1_out, ResultToLess_p9);
  Clock clock_1 (.out(clock_1_out));
  Register PC (.D(multiplexer_5_out), .en(not_1_out), .Q(PC_q), .clk(clock_1_out), .clr(button_1_out));
  Button button_1 (.out(button_1_out));
  Adder adder_1 (.a(PC_q), .b(8'h1), .out(adder_1_out));  // open: cin, cout
  ROM #(.dataWidth(16)) rom_1 (.addr(PC_q), .data(rom_1_data), .sel(1'b1));
  IF_ID_Buffer IF_ID_Buffer (.in_1(rom_1_data), .ClockIn(clock_1_out), .out_3(IF_ID_Buffer_out_3));
  // InstructionSplitter Instruction_Splitter: pin names not known; wires that end beside it: IF_ID_Buffer_out_3, Instruction_Splitter_p2, Instruction_Splitter_p3, Instruction_Splitter_p4, Instruction_Splitter_p5, Instruction_Splitter_p6, Instruction_Splitter_p7, Instruction_Splitter_p8, Instruction_Splitter_p9
  // ResultToLess ResultToLess: pin names not known; wires that end beside it: ResultToLess_p1, ResultToLess_p2, Instruction_Splitter_p2, Instruction_Splitter_p7, ResultToLess_p5, ResultToLess_p2, ResultToLess_p7, ResultToLess_p8, ResultToLess_p9, ResultToLess_p10, ResultToLess_p11, ResultToLess_p12, ResultToLess_p13
  // SignExtend Sign_Extend: pin names not known; wires that end beside it: Instruction_Splitter_p8, Instruction_Splitter_p9, Sign_Extend_p3
  // Decoder Decoder: pin names not known; wires that end beside it: Decoder_p1, Decoder_p2, Decoder_p3, Decoder_p4, Decoder_p5, Decoder_p6, Decoder_p7, Decoder_p8
  // RegisterFile Registers: pin names not known; wires that end beside it: Instruction_Splitter_p3, Instruction_Splitter_p4, Instruction_Splitter_p5, Registers_p4, Decoder_p3, clock_1_out, Registers_p7, Registers_p8
  ID_EX_Buffer ID_EX_Buffer (
    .in_1(adder_1_out), .CLK(clock_1_out), .in_3(Instruction_Splitter_p9), .in_4(Registers_p7),
    .in_5(Registers_p8), .in_6(Registers_p8), .in_7(Sign_Extend_p3), .in_9(Instruction_Splitter_p7),
    .in_10(Registers_p7), .in_11(Registers_p8), .in_12(Decoder_p1), .in_13(Instruction_Splitter_p6),
    .in_14(adder_1_out), .in_15(Decoder_p2), .in_17(Decoder_p4), .in_18(Decoder_p5), .in_19(Decoder_p6),
    .in_20(Decoder_p7), .in_21(Decoder_p8), .in_22(ResultToLess_p7), .in_23(ResultToLess_p8),
    .in_24(ResultToLess_p10), .in_25(ResultToLess_p11), .in_26(ResultToLess_p12), .in_27(ResultToLess_p13),
    .out_28(ID_EX_Buffer_out_28), .out_29(ID_EX_Buffer_out_29), .out_30(ID_EX_Buffer_out_30),
    .out_31(ID_EX_Buffer_out_31), .out_32(ID_EX_Buffer_out_32), .out_33(Registers_p8),
    .out_35(ID_EX_Buffer_out_35), .out_36(ID_EX_Buffer_out_36), .out_37(ID_EX_Buffer_out_37),
    .out_38(ID_EX_Buffer_out_38), .out_39(ID_EX_Buffer_out_39), .out_40(ID_EX_Buffer_out_40),
    .out_41(ID_EX_Buffer_out_41), .out_43(ID_EX_Buffer_out_43), .out_44(ID_EX_Buffer_out_44),
    .out_45(ID_EX_Buffer_out_45), .out_46(ID_EX_Buffer_out_46), .out_48(ID_EX_Buffer_out_48),
    .out_49(ID_EX_Buffer_out_49), .out_50(ID_EX_Buffer_out_50), .out_51(ID_EX_Buffer_out_51),
    .out_52(ID_EX_Buffer_out_52), .out_53(ID_EX_Buffer_out_53));  // open: in_8, in_16, out_34, out_42, out_47
  Multiplexer #(.select(2), .width(16), .disabled(0), .enable("false")) multiplexer_1 (
    .in0(ID_EX_Buffer_out_30), .in1(Registers_p4), .in2(ex_mem_buffer_1_read_data_1_3),
    .out(multiplexer_1_out), .sel(undriven));  // open: in3
  Multiplexer #(.select(2), .width(16), .disabled(0), .enable("false")) multiplexer_2 (
    .in0(ID_EX_Buffer_out_31), .in1(Registers_p4), .in2(ex_mem_buffer_1_read_data_1_3),
    .out(multiplexer_2_out), .sel(undriven_2));  // open: in3
  // ALUtoPC RegistertoAddress: pin names not known; wires that end beside it: ID_EX_Buffer_out_30, RegistertoAddress_p2
  Multiplexer #(.width(16), .disabled(0), .enable("false")) multiplexer_3 (
    .in0(multiplexer_2_out), .in1(Registers_p8), .out(multiplexer_3_out), .sel(ID_EX_Buffer_out_44));
  Multiplexer #(.width(8), .disabled(0), .enable("false")) multiplexer_4 (
    .in0(ID_EX_Buffer_out_28), .in1(ID_EX_Buffer_out_29), .out(multiplexer_4_out), .sel(ID_EX_Buffer_out_46));
  ALU alu_1 (
    .ALU_Op(ID_EX_Buffer_out_43), .Input_A(multiplexer_1_out), .Input_B(multiplexer_3_out),
    .Zero(ResultToLess_p5), .ALU_Output(alu_1_alu_output));  // open: BorrowOut
  EX_MEM_Buffer ex_mem_buffer_1 (
    .CLK(clock_1_out), .in_2(multiplexer_4_out), .in_3(RegistertoAddress_p2), .in_4(alu_1_alu_output),
    .in_5(ID_EX_Buffer_out_32), .in_6(ID_EX_Buffer_out_41), .in_7(ID_EX_Buffer_out_36),
    .in_8(ID_EX_Buffer_out_35), .in_9(ID_EX_Buffer_out_37), .in_10(ID_EX_Buffer_out_38),
    .in_11(ID_EX_Buffer_out_39), .in_12(ID_EX_Buffer_out_40), .in_13(ID_EX_Buffer_out_45),
    .in_14(ID_EX_Buffer_out_48), .in_15(ID_EX_Buffer_out_49), .in_16(ID_EX_Buffer_out_50),
    .in_17(ID_EX_Buffer_out_51), .in_18(ID_EX_Buffer_out_53), .in_19(ID_EX_Buffer_out_52),
    .out_21(ex_mem_buffer_1_out_21), .Read_Data_1(ex_mem_buffer_1_read_data_1),
    .Read_Data_1_2(ResultToLess_p1), .Read_Data_1_3(ex_mem_buffer_1_read_data_1_3),
    .Read_Data_1_4(ex_mem_buffer_1_read_data_1_4), .Read_Data_1_5(ex_mem_buffer_1_read_data_1_5),
    .Read_Data_1_6(ex_mem_buffer_1_read_data_1_6), .Read_Data_1_7(ex_mem_buffer_1_read_data_1_7),
    .Read_Data_1_8(ex_mem_buffer_1_read_data_1_8), .Read_Data_1_9(ex_mem_buffer_1_read_data_1_9),
    .Read_Data_1_10(ex_mem_buffer_1_read_data_1_10), .Read_Data_1_11(ex_mem_buffer_1_read_data_1_11),
    .Read_Data_1_12(ex_mem_buffer_1_read_data_1_12), .Read_Data_1_13(ex_mem_buffer_1_read_data_1_13),
    .Read_Data_1_14(ex_mem_buffer_1_read_data_1_14), .Read_Data_1_15(ex_mem_buffer_1_read_data_1_15),
    .Read_Data_1_16(ex_mem_buffer_1_read_data_1_16), .Read_Data_1_17(ex_mem_buffer_1_read_data_1_17));  // open: in_20, Read_Data_1_18
  Multiplexer #(.width(8), .disabled(0), .enable("false")) multiplexer_5 (
    .in0(ex_mem_buffer_1_out_21), .in1(ex_mem_buffer_1_read_data_1), .out(multiplexer_5_out),
    .sel(ex_mem_buffer_1_read_data_1_11));
  // ALUtoPC RegistertoAddress_2: pin names not known; wires that end beside it: ex_mem_buffer_1_read_data_1_3, RegistertoAddress_2_p2
  Multiplexer #(.width(16), .disabled(0), .enable("false")) multiplexer_6 (
    .in0(multiplexer_7_out), .in1(bit_extender_1_out), .out(Registers_p4),
    .sel(ex_mem_buffer_1_read_data_1_16));
  // Shifter Shifter: pin names not known; wires that end beside it: ex_mem_buffer_1_read_data_1_6, ex_mem_buffer_1_read_data_1_5, ex_mem_buffer_1_read_data_1_7, ex_mem_buffer_1_read_data_1_8, ex_mem_buffer_1_read_data_1_9, Shifter_p6
  assign bit_extender_1_out = {{8{1'b0}}, ex_mem_buffer_1_read_data_1_10};  // Bit_Extender bit_extender_1
  Multiplexer #(.width(16), .disabled(0), .enable("false")) multiplexer_7 (
    .in0(multiplexer_8_out), .in1(Shifter_p6), .out(multiplexer_7_out), .sel(ex_mem_buffer_1_read_data_1_4));
  RAM #(.dataWidth(16), .bus("separate")) ram_1 (
    .addr(RegistertoAddress_2_p2), .din(ex_mem_buffer_1_read_data_1_5), .data(ram_1_data),
    .str(ex_mem_buffer_1_read_data_1_12), .sel(1'b1), .clk(clock_1_out), .ld(ex_mem_buffer_1_read_data_1_17));  // open: clr
  MEM_WB_Buffer mem_wb_buffer_1 (
    .CLK(clock_1_out), .in_2(ResultToLess_p1), .in_3(ram_1_data), .in_4(ex_mem_buffer_1_read_data_1_13),
    .in_5(ex_mem_buffer_1_read_data_1_5), .in_6(ex_mem_buffer_1_read_data_1_15),
    .in_7(ex_mem_buffer_1_read_data_1_14), .out_8(mem_wb_buffer_1_out_8), .out_9(mem_wb_buffer_1_out_9),
    .out_10(mem_wb_buffer_1_out_10), .out_11(mem_wb_buffer_1_out_11), .out_12(mem_wb_buffer_1_out_12),
    .out_13(mem_wb_buffer_1_out_13));
  Multiplexer #(.width(16), .disabled(0), .enable("false")) multiplexer_8 (
    .in0(mem_wb_buffer_1_out_8), .in1(mem_wb_buffer_1_out_9), .out(multiplexer_8_out),
    .sel(mem_wb_buffer_1_out_10));
  Register #(.width(16)) register_1 (
    .D(mem_wb_buffer_1_out_11), .en(mem_wb_buffer_1_out_12), .Q(register_1_q), .clk(clock_1_out));  // open: clr
  Hex_Digit_Display hex_digit_display_1 (.value(register_1_q[15:12]));  // open: dp
  Hex_Digit_Display hex_digit_display_2 (.value(register_1_q[11:8]));  // open: dp
  LED Halt (.in(mem_wb_buffer_1_out_13));
  Hex_Digit_Display hex_digit_display_3 (.value(register_1_q[3:0]));  // open: dp
  Hex_Digit_Display hex_digit_display_4 (.value(register_1_q[7:4]));  // open: dp

  // Notes on the sheet:
  //   contents of rom_1 (hex, n*v repeats v):
  //   1 1104 241 1303 40 f000 241 1300 481 1503 281 6c1 1705 2c1 f200 901 1900 18ff f800 b41 1bf0 1b0f
  //   fa00 d81 1d19 fc1 1f20 3dc0 fc00 1 11e0 241 1378 3041 f000 481 150d 6c1 1708 44c0 f400 901 1910 b41
  //   1b04 4941 f800 d81 1d02 5c02 fc00 fc1 1f10 5e03 fe00 1 1140 61c1 63c0 f200 481 15ff 6c1 1701 845b
  //   865b 901 1900 985f b41 1b00 d81 1d00 1ce9 aa63 ac63 fc1 1f00 1 1119 be67 b067 e054 7000 c259 6c1
  //   170a f600 7000 d200 7000 fc1 1f01 fe00 7000 fc1 1f02 fe00 7000 fc1 1f03 fe00 7000 fc1 1f04 fe00 7000
  //   ID/EX Buffer
  //   ALU_MUXA
  //   ALU_MUXB
  //   (Forwarding Unit)
  //   Imm
  //   ALU_MUXA SEL
  //   ALU_MUXB SEL
  //   ALU_MUXC SEL
  //   (MUX C resolves ld -> sd)
  //   EX/MEM Buffer
  //   MEM/WB Buffer
endmodule

module IF_ID_Buffer (
  input  [15:0] in_1,
  input  ClockIn,
  output [15:0] out_3
);

  Register #(.width(16)) Instruction_Memory (.D(in_1), .Q(out_3), .clk(ClockIn));  // open: en, clr
endmodule

module ID_EX_Buffer (
  input  [7:0] in_1,
  input  CLK,
  input  [7:0] in_3,
  input  [15:0] in_4,
  input  [15:0] in_5,
  input  [15:0] in_6,
  input  [15:0] in_7,
  input  [15:0] in_8,
  input  in_9,
  input  [15:0] in_10,
  input  [15:0] in_11,
  input  in_12,
  input  [3:0] in_13,
  input  [7:0] in_14,
  input  in_15,
  input  in_16,
  input  [3:0] in_17,
  input  in_18,
  input  in_19,
  input  in_20,
  input  in_21,
  input  in_22,
  input  in_23,
  input  in_24,
  input  in_25,
  input  in_26,
  input  in_27,
  output [7:0] out_28,
  output [7:0] out_29,
  output [15:0] out_30,
  output [15:0] out_31,
  output [15:0] out_32,
  output [15:0] out_33,
  output [15:0] out_34,
  output out_35,
  output [15:0] out_36,
  output [15:0] out_37,
  output out_38,
  output [3:0] out_39,
  output [7:0] out_40,
  output out_41,
  output out_42,
  output [3:0] out_43,
  output out_44,
  output out_45,
  output out_46,
  output out_47,
  output out_48,
  output out_49,
  output out_50,
  output out_51,
  output out_52,
  output out_53
);

  Register register_1 (.D(in_1), .Q(out_28), .clk(CLK));  // open: en, clr
  Register register_2 (.D(in_3), .Q(out_29), .clk(CLK));  // open: en, clr
  Register #(.width(16)) register_3 (.D(in_4), .Q(out_30), .clk(CLK));  // open: en, clr
  Register #(.width(16)) register_4 (.D(in_5), .Q(out_31), .clk(CLK));  // open: en, clr
  Register #(.width(16)) register_5 (.D(in_6), .Q(out_32), .clk(CLK));  // open: en, clr
  Register #(.width(16)) register_6 (.D(in_7), .Q(out_33), .clk(CLK));  // open: en, clr
  Register #(.width(16)) register_7 (.D(in_8), .Q(out_34), .clk(CLK));  // open: en, clr
  Register #(.width(1)) register_8 (.D(in_9), .Q(out_35), .clk(CLK));  // open: en, clr
  Register #(.width(16)) register_9 (.D(in_10), .Q(out_36), .clk(CLK));  // open: en, clr
  Register #(.width(16)) register_10 (.D(in_11), .Q(out_37), .clk(CLK));  // open: en, clr
  Register #(.width(1)) register_11 (.D(in_12), .Q(out_38), .clk(CLK));  // open: en, clr
  Register #(.width(4)) register_12 (.D(in_13), .Q(out_39), .clk(CLK));  // open: en, clr
  Register register_13 (.D(in_14), .Q(out_40), .clk(CLK));  // open: en, clr
  Register #(.width(1)) register_14 (.D(in_15), .Q(out_41), .clk(CLK));  // open: en, clr
  Register #(.width(1)) register_15 (.D(in_16), .Q(out_42), .clk(CLK));  // open: en, clr
  Register #(.width(4)) register_16 (.D(in_17), .Q(out_43), .clk(CLK));  // open: en, clr
  Register #(.width(1)) register_17 (.D(in_18), .Q(out_44), .clk(CLK));  // open: en, clr
  Register #(.width(1)) register_18 (.D(in_19), .Q(out_45), .clk(CLK));  // open: en, clr
  Register #(.width(1)) register_19 (.D(in_20), .Q(out_46), .clk(CLK));  // open: en, clr
  Register #(.width(1)) register_20 (.D(in_21), .Q(out_47), .clk(CLK));  // open: en, clr
  Register #(.width(1)) register_21 (.D(in_22), .Q(out_48), .clk(CLK));  // open: en, clr
  Register #(.width(1)) register_22 (.D(in_23), .Q(out_49), .clk(CLK));  // open: en, clr
  Register #(.width(1)) register_23 (.D(in_24), .Q(out_50), .clk(CLK));  // open: en, clr
  Register #(.width(1)) register_24 (.D(in_25), .Q(out_51), .clk(CLK));  // open: en, clr
  Register #(.width(1)) register_25 (.D(in_26), .Q(out_52), .clk(CLK));  // open: en, clr
  Register #(.width(1)) register_26 (.D(in_27), .Q(out_53), .clk(CLK));  // open: en, clr
endmodule

module EX_MEM_Buffer (
  input  CLK,
  input  [7:0] in_2,
  input  [7:0] in_3,
  input  [15:0] in_4,
  input  [15:0] in_5,
  input  in_6,
  input  [15:0] in_7,
  input  in_8,
  input  [15:0] in_9,
  input  in_10,
  input  [3:0] in_11,
  input  [7:0] in_12,
  input  in_13,
  input  in_14,
  input  in_15,
  input  in_16,
  input  in_17,
  input  in_18,
  input  in_19,
  input  [15:0] in_20,
  output [7:0] out_21,
  output [7:0] Read_Data_1,
  output [15:0] Read_Data_1_2,
  output [15:0] Read_Data_1_3,
  output Read_Data_1_4,
  output [15:0] Read_Data_1_5,
  output Read_Data_1_6,
  output [15:0] Read_Data_1_7,
  output Read_Data_1_8,
  output [3:0] Read_Data_1_9,
  output [7:0] Read_Data_1_10,
  output Read_Data_1_11,
  output Read_Data_1_12,
  output Read_Data_1_13,
  output Read_Data_1_14,
  output Read_Data_1_15,
  output Read_Data_1_16,
  output Read_Data_1_17,
  output [15:0] Read_Data_1_18
);

  Register register_1 (.D(in_2), .Q(out_21), .clk(CLK));  // open: en, clr
  Register register_2 (.D(in_3), .Q(Read_Data_1), .clk(CLK));  // open: en, clr
  Register #(.width(16)) register_3 (.D(in_4), .Q(Read_Data_1_2), .clk(CLK));  // open: en, clr
  Register #(.width(16)) register_4 (.D(in_5), .Q(Read_Data_1_3), .clk(CLK));  // open: en, clr
  Register #(.width(1)) register_5 (.D(in_6), .Q(Read_Data_1_4), .clk(CLK));  // open: en, clr
  Register #(.width(16)) register_6 (.D(in_7), .Q(Read_Data_1_5), .clk(CLK));  // open: en, clr
  Register #(.width(1)) register_7 (.D(in_8), .Q(Read_Data_1_6), .clk(CLK));  // open: en, clr
  Register #(.width(16)) register_8 (.D(in_9), .Q(Read_Data_1_7), .clk(CLK));  // open: en, clr
  Register #(.width(1)) register_9 (.D(in_10), .Q(Read_Data_1_8), .clk(CLK));  // open: en, clr
  Register #(.width(4)) register_10 (.D(in_11), .Q(Read_Data_1_9), .clk(CLK));  // open: en, clr
  Register register_11 (.D(in_12), .Q(Read_Data_1_10), .clk(CLK));  // open: en, clr
  Register #(.width(1)) register_12 (.D(in_13), .Q(Read_Data_1_11), .clk(CLK));  // open: en, clr
  Register #(.width(1)) register_13 (.D(in_14), .Q(Read_Data_1_12), .clk(CLK));  // open: en, clr
  Register #(.width(1)) register_14 (.D(in_15), .Q(Read_Data_1_13), .clk(CLK));  // open: en, clr
  Register #(.width(1)) register_15 (.D(in_16), .Q(Read_Data_1_14), .clk(CLK));  // open: en, clr
  Register #(.width(1)) register_16 (.D(in_17), .Q(Read_Data_1_15), .clk(CLK));  // open: en, clr
  Register #(.width(1)) register_17 (.D(in_18), .Q(Read_Data_1_16), .clk(CLK));  // open: en, clr
  Register #(.width(1)) register_18 (.D(in_19), .en(in_19), .Q(Read_Data_1_17), .clk(CLK));  // open: clr
  Register #(.width(16)) register_19 (.D(in_20), .Q(Read_Data_1_18), .clk(CLK));  // open: en, clr
endmodule

module MEM_WB_Buffer (
  input  CLK,
  input  [15:0] in_2,
  input  [15:0] in_3,
  input  in_4,
  input  [15:0] in_5,
  input  in_6,
  input  in_7,
  output [15:0] out_8,
  output [15:0] out_9,
  output out_10,
  output [15:0] out_11,
  output out_12,
  output out_13
);

  Register #(.width(16)) register_1 (.D(in_2), .Q(out_8), .clk(CLK));  // open: en, clr
  Register #(.width(16)) register_2 (.D(in_3), .Q(out_9), .clk(CLK));  // open: en, clr
  Register #(.width(1)) register_3 (.D(in_4), .Q(out_10), .clk(CLK));  // open: en, clr
  Register #(.width(16)) register_4 (.D(in_5), .Q(out_11), .clk(CLK));  // open: en, clr
  Register #(.width(1)) register_5 (.D(in_6), .Q(out_12), .clk(CLK));  // open: en, clr
  Register #(.width(1)) register_6 (.D(in_7), .Q(out_13), .clk(CLK));  // open: en, clr
endmodule
